// Logisim project bending-machine.circ as structural Verilog: 6 circuits, main circuit main
module main (
  output [7:0] out_1,
  output [7:0] out_2
);

  wire \_100원_out , \_500원_out , \_1000원_out , and_1_out, comparator_1_lt, n7_segment_1_a, n7_segment_1_b,
       n7_segment_1_c, n7_segment_1_d, n7_segment_1_e, n7_segment_1_f, n7_segment_1_g, n7_segment_2_a,
       n7_segment_2_b, n7_segment_2_c, n7_segment_2_d, n7_segment_2_e, n7_segment_2_f, n7_segment_2_g,
       n7_segment_3_a, n7_segment_3_b, n7_segment_3_c, n7_segment_3_d, n7_segment_3_e, n7_segment_3_f,
       n7_segment_3_g, n7_segment_4_a, n7_segment_4_b, n7_segment_4_c, n7_segment_4_d, n7_segment_4_e,
       n7_segment_4_f, n7_segment_4_g, not_1_out, not_2_out, \가격표시등_1_out_2 , \가격표시등_1_out_3 ,
       \가격표시등_1_out_4 , \가격표시등_1_out_5 , \가격표시등_1_out_6 , \가격표시등_1_out_7 , \가격표시등_1_out_8 , \가격표시등_1_out_9 ,
       \가격표시등_1_out_10 , \가격표시등_1_out_11 , \가격표시등_1_out_12 , \가격표시등_1_out_13 , \가격표시등_1_out_14 ,
       \가격표시등_1_out_15 , \가격표시등_1_out_16 , \가격표시등_1_out_17 , \동전_투입_1_out_6 , \맥스_out , \미닛에이드_out ,
       \버튼_led_조명_1_맥스 , \버튼_led_조명_1_물 , \버튼_led_조명_1_코코팜 , \버튼_led_조명_1_토레타 , \버튼_led_조명_1_파워에이드 ,
       \음료_선택_1_out_7 , \초기화_out , \코코팜_out , \토레타_out , \파워에이드_out ;
  wire [7:0] multiplexer_1_out, subtractor_1_out, \동전_투입_1_out_5 , \음료_선택_1_out_6 ;

  Button \_100원  (.out(\_100원_out ));
  Button \_500원  (.out(\_500원_out ));
  Button \_1000원  (.out(\_1000원_out ));
  \동전_투입  \u_동전_투입_1  (
    .in_1(out_1), .\_100원 (\_100원_out ), .\_500원 (\_500원_out ), .\_1000원 (\_1000원_out ),
    .out_5(\동전_투입_1_out_5 ), .out_6(\동전_투입_1_out_6 ));
  Button \u_미닛에이드  (.out(\미닛에이드_out ));
  LED led_1 (.in(\버튼_led_조명_1_물 ));
  Multiplexer #(.width(8)) multiplexer_1 (
    .in0(\동전_투입_1_out_5 ), .in1(out_2), .out(multiplexer_1_out), .sel(not_1_out));  // open: en
  not not_1 (not_1_out, \음료_선택_1_out_7 );
  \음료_선택  \u_음료_선택_1  (
    .\미닛메이드 (\미닛에이드_out ), .\맥스 (\맥스_out ), .\코코팜 (\코코팜_out ), .\파워에이드 (\파워에이드_out ), .\토레타 (\토레타_out ),
    .out_6(\음료_선택_1_out_6 ), .out_7(\음료_선택_1_out_7 ));
  Button \u_맥스  (.out(\맥스_out ));
  Button \u_코코팜  (.out(\코코팜_out ));
  LED led_2 (.in(\버튼_led_조명_1_맥스 ));
  LED led_3 (.in(\버튼_led_조명_1_코코팜 ));
  and and_1 (and_1_out, \동전_투입_1_out_6 , \음료_선택_1_out_7 );
  Button \u_초기화  (.out(\초기화_out ));
  Button \u_파워에이드  (.out(\파워에이드_out ));
  LED led_4 (.in(\버튼_led_조명_1_파워에이드 ));
  \버튼_LED_조명  \u_버튼_led_조명_1  (
    .in_1(out_2), .\토레타 (\버튼_led_조명_1_토레타 ), .\파워에이드 (\버튼_led_조명_1_파워에이드 ), .\맥스 (\버튼_led_조명_1_맥스 ),
    .\코코팜 (\버튼_led_조명_1_코코팜 ), .\물 (\버튼_led_조명_1_물 ));
  Register register_1 (.D(multiplexer_1_out), .Q(out_1), .clk(and_1_out), .clr(\초기화_out ));  // open: en
  Button \u_토레타  (.out(\토레타_out ));
  LED led_5 (.in(\버튼_led_조명_1_토레타 ));
  Subtractor subtractor_1 (.a(out_1), .b(\음료_선택_1_out_6 ), .out(subtractor_1_out));  // open: bin, bout
  Multiplexer #(.width(8)) multiplexer_2 (
    .in0(out_1), .in1(subtractor_1_out), .out(out_2), .sel(not_2_out));  // open: en
  not not_2 (not_2_out, comparator_1_lt);
  Comparator comparator_1 (.a(subtractor_1_out), .b({8{1'b0}}), .lt(comparator_1_lt));  // open: gt, eq
  \가격표시등  \u_가격표시등_1  (
    .in_1(out_2), .out_2(\가격표시등_1_out_2 ), .out_3(\가격표시등_1_out_3 ), .out_4(\가격표시등_1_out_4 ),
    .out_5(\가격표시등_1_out_5 ), .out_6(\가격표시등_1_out_6 ), .out_7(\가격표시등_1_out_7 ), .out_8(\가격표시등_1_out_8 ),
    .out_9(\가격표시등_1_out_9 ), .out_10(\가격표시등_1_out_10 ), .out_11(\가격표시등_1_out_11 ), .out_12(\가격표시등_1_out_12 ),
    .out_13(\가격표시등_1_out_13 ), .out_14(\가격표시등_1_out_14 ), .out_15(\가격표시등_1_out_15 ),
    .out_16(\가격표시등_1_out_16 ), .out_17(\가격표시등_1_out_17 ));
  _7_Segment_Display u_7_segment_display_1 (
    .g(n7_segment_1_g), .f(n7_segment_1_f), .a(n7_segment_1_a), .b(n7_segment_1_b), .e(n7_segment_1_e),
    .d(n7_segment_1_d), .c(n7_segment_1_c));  // open: dp
  _7_segment u_7_segment_1 (
    .w(\가격표시등_1_out_2 ), .x(\가격표시등_1_out_3 ), .y(\가격표시등_1_out_4 ), .z(\가격표시등_1_out_5 ), .a(n7_segment_1_a),
    .b(n7_segment_1_b), .c(n7_segment_1_c), .d(n7_segment_1_d), .e(n7_segment_1_e), .f(n7_segment_1_f),
    .g(n7_segment_1_g));
  _7_segment u_7_segment_2 (
    .w(\가격표시등_1_out_6 ), .x(\가격표시등_1_out_7 ), .y(\가격표시등_1_out_8 ), .z(\가격표시등_1_out_9 ), .a(n7_segment_2_a),
    .b(n7_segment_2_b), .c(n7_segment_2_c), .d(n7_segment_2_d), .e(n7_segment_2_e), .f(n7_segment_2_f),
    .g(n7_segment_2_g));
  _7_segment u_7_segment_3 (
    .w(\가격표시등_1_out_10 ), .x(\가격표시등_1_out_11 ), .y(\가격표시등_1_out_12 ), .z(\가격표시등_1_out_13 ),
    .a(n7_segment_3_a), .b(n7_segment_3_b), .c(n7_segment_3_c), .d(n7_segment_3_d), .e(n7_segment_3_e),
    .f(n7_segment_3_f), .g(n7_segment_3_g));
  _7_segment u_7_segment_4 (
    .w(\가격표시등_1_out_14 ), .x(\가격표시등_1_out_15 ), .y(\가격표시등_1_out_16 ), .z(\가격표시등_1_out_17 ),
    .a(n7_segment_4_a), .b(n7_segment_4_b), .c(n7_segment_4_c), .d(n7_segment_4_d), .e(n7_segment_4_e),
    .f(n7_segment_4_f), .g(n7_segment_4_g));
  _7_Segment_Display u_7_segment_display_2 (
    .g(n7_segment_2_g), .f(n7_segment_2_f), .a(n7_segment_2_a), .b(n7_segment_2_b), .e(n7_segment_2_e),
    .d(n7_segment_2_d), .c(n7_segment_2_c));  // open: dp
  _7_Segment_Display u_7_segment_display_3 (
    .g(n7_segment_3_g), .f(n7_segment_3_f), .a(n7_segment_3_a), .b(n7_segment_3_b), .e(n7_segment_3_e),
    .d(n7_segment_3_d), .c(n7_segment_3_c));  // open: dp
  _7_Segment_Display u_7_segment_display_4 (
    .g(n7_segment_4_g), .f(n7_segment_4_f), .a(n7_segment_4_a), .b(n7_segment_4_b), .e(n7_segment_4_e),
    .d(n7_segment_4_d), .c(n7_segment_4_c));  // open: dp

  // Notes on the sheet:
  //   자판기 ver 1
  //   github.com/SimDaSong
  //   600원
  //   800원
  //   800원
  //   1000원
  //   1600원
endmodule

module \동전_투입  (
  input  [7:0] in_1,
  input  \_100원 ,
  input  \_500원 ,
  input  \_1000원 ,
  output [7:0] out_5,
  output out_6
);

  wire comparator_1_lt, not_1_out;
  wire [1:0] controlled_buffer_1_out;
  wire [7:0] adder_1_out, multiplexer_1_out;

  assign controlled_buffer_1_out = out_6 ? 2'b00 : 2'bz;  // Controlled_Buffer controlled_buffer_1
  assign controlled_buffer_1_out = \_100원  ? 2'b01 : 2'bz;  // Controlled_Buffer controlled_buffer_2
  assign controlled_buffer_1_out = \_500원  ? 2'b10 : 2'bz;  // Controlled_Buffer controlled_buffer_3
  assign controlled_buffer_1_out = \_1000원  ? 2'b11 : 2'bz;  // Controlled_Buffer controlled_buffer_4
  Multiplexer #(.select(2), .width(8)) multiplexer_1 (
    .in0({8{1'b0}}), .in1(8'h1), .in2(8'h5), .in3(8'ha), .out(multiplexer_1_out),
    .sel(controlled_buffer_1_out));  // open: en
  Adder adder_1 (.a(in_1), .b(multiplexer_1_out), .out(adder_1_out));  // open: cin, cout
  nor nor_1 (out_6, \_100원 , \_500원 , \_1000원 );
  Comparator comparator_1 (.a(adder_1_out), .b(8'h64), .lt(comparator_1_lt));  // open: gt, eq
  Multiplexer #(.width(8)) multiplexer_2 (.in0(adder_1_out), .in1(in_1), .out(out_5), .sel(not_1_out));  // open: en
  not not_1 (not_1_out, comparator_1_lt);

  // Notes on the sheet:
  //   동전 투입
endmodule

module \음료_선택  (
  input  \미닛메이드 ,
  input  \맥스 ,
  input  \코코팜 ,
  input  \파워에이드 ,
  input  \토레타 ,
  output [7:0] out_6,
  output out_7
);

  wire [3:0] controlled_buffer_1_out;

  assign controlled_buffer_1_out = out_7 ? 4'b0000 : 4'bz;  // Controlled_Buffer controlled_buffer_1
  assign controlled_buffer_1_out = \미닛메이드  ? 4'b0001 : 4'bz;  // Controlled_Buffer controlled_buffer_2
  assign controlled_buffer_1_out = \맥스  ? 4'b0010 : 4'bz;  // Controlled_Buffer controlled_buffer_3
  assign controlled_buffer_1_out = \코코팜  ? 4'b0011 : 4'bz;  // Controlled_Buffer controlled_buffer_4
  assign controlled_buffer_1_out = \파워에이드  ? 4'b0100 : 4'bz;  // Controlled_Buffer controlled_buffer_5
  assign controlled_buffer_1_out = \토레타  ? 4'b0101 : 4'bz;  // Controlled_Buffer controlled_buffer_6
  ROM #(.addrWidth(4)) rom_1 (.addr(controlled_buffer_1_out), .data(out_6));  // open: sel
  nor nor_1 (out_7, \미닛메이드 , \맥스 , \코코팜 , \파워에이드 , \토레타 );

  // Notes on the sheet:
  //   음료 선택
  //   contents of rom_1 (hex, n*v repeats v):
  //   0 6 8 8 a 10
endmodule

module \버튼_LED_조명  (
  input  [7:0] in_1,
  output \토레타 ,
  output \파워에이드 ,
  output \맥스 ,
  output \코코팜 ,
  output \물 
);

  wire comparator_1_lt, comparator_2_lt, comparator_3_lt, comparator_4_lt;

  Comparator comparator_1 (.a(in_1), .b(8'hf), .lt(comparator_1_lt));  // open: gt, eq
  not not_1 (\토레타 , comparator_1_lt);
  Comparator comparator_2 (.a(in_1), .b(8'ha), .lt(comparator_2_lt));  // open: gt, eq
  not not_2 (\파워에이드 , comparator_2_lt);
  Comparator comparator_3 (.a(in_1), .b(8'h8), .lt(comparator_3_lt));  // open: gt, eq
  not not_3 (\맥스 , comparator_3_lt);
  Comparator comparator_4 (.a(in_1), .b(8'h6), .lt(comparator_4_lt));  // open: gt, eq
  not not_4 (\물 , comparator_4_lt);

  assign \코코팜  = \맥스 ;

  // Notes on the sheet:
  //   버튼 LED 조명
endmodule

module _7_segment (
  input  w,
  input  x,
  input  y,
  input  z,
  output a,
  output b,
  output c,
  output d,
  output e,
  output f,
  output g
);

  wire and_1_out, and_2_out, and_3_out, and_4_out, and_5_out, and_6_out, and_7_out, and_8_out, and_9_out,
       and_10_out, and_11_out, and_12_out, and_13_out, and_14_out, and_15_out, and_16_out, and_17_out,
       and_18_out, and_19_out, and_20_out, and_21_out, and_22_out, and_23_out, and_24_out, and_25_out,
       and_26_out, not_1_out, not_2_out, not_3_out, not_4_out, not_5_out, not_6_out, not_7_out, not_8_out,
       not_9_out, not_10_out, not_11_out, not_12_out, not_13_out, not_14_out, not_15_out, not_16_out,
       not_17_out, not_18_out, not_19_out, not_20_out, not_21_out, not_22_out, not_23_out, not_24_out,
       not_25_out, not_26_out, not_27_out, not_28_out, not_29_out, not_30_out, not_31_out, not_32_out,
       not_33_out;

  not not_1 (not_1_out, x);
  and and_1 (and_1_out, not_1_out, not_2_out);
  not not_2 (not_2_out, z);
  not not_3 (not_3_out, w);
  and and_2 (and_2_out, not_3_out, y);
  not not_4 (not_4_out, w);
  and and_3 (and_3_out, not_4_out, x, z);
  and and_4 (and_4_out, w, not_5_out);
  not not_5 (not_5_out, x);
  and and_5 (and_5_out, w, not_6_out);
  not not_6 (not_6_out, y);
  and and_6 (and_6_out, w, not_7_out);
  not not_7 (not_7_out, z);
  not not_8 (not_8_out, x);
  not not_9 (not_9_out, y);
  and and_7 (and_7_out, not_9_out, not_10_out);
  not not_10 (not_10_out, z);
  not not_11 (not_11_out, w);
  and and_8 (and_8_out, not_11_out, y, z);
  not not_12 (not_12_out, y);
  not not_13 (not_13_out, x);
  and and_9 (and_9_out, not_13_out, z);
  not not_14 (not_14_out, w);
  and and_10 (and_10_out, not_14_out, x);
  and and_11 (and_11_out, x, not_15_out);
  not not_15 (not_15_out, z);
  not not_16 (not_16_out, x);
  and and_12 (and_12_out, not_16_out, not_17_out);
  not not_17 (not_17_out, z);
  not not_18 (not_18_out, x);
  and and_13 (and_13_out, not_18_out, y);
  and and_14 (and_14_out, y, not_19_out);
  not not_19 (not_19_out, z);
  and and_15 (and_15_out, x, not_20_out, z);
  not not_20 (not_20_out, y);
  not not_21 (not_21_out, x);
  and and_16 (and_16_out, not_21_out, not_22_out);
  not not_22 (not_22_out, z);
  and and_17 (and_17_out, y, not_23_out);
  not not_23 (not_23_out, z);
  not not_24 (not_24_out, y);
  and and_18 (and_18_out, not_24_out, not_25_out);
  not not_25 (not_25_out, z);
  not not_26 (not_26_out, w);
  and and_19 (and_19_out, not_26_out, x);
  and and_20 (and_20_out, w, not_27_out);
  not not_27 (not_27_out, x);
  and and_21 (and_21_out, w, not_28_out);
  not not_28 (not_28_out, y);
  and and_22 (and_22_out, w, not_29_out);
  not not_29 (not_29_out, z);
  not not_30 (not_30_out, x);
  and and_23 (and_23_out, not_30_out, y);
  and and_24 (and_24_out, x, not_31_out);
  not not_31 (not_31_out, y);
  and and_25 (and_25_out, x, not_32_out);
  not not_32 (not_32_out, z);
  and and_26 (and_26_out, w, not_33_out);
  not not_33 (not_33_out, x);
  or or_1 (b, not_8_out, and_7_out, and_8_out);
  or or_2 (c, not_12_out, and_9_out, and_10_out, and_11_out);
  or or_3 (d, and_12_out, and_13_out, and_14_out, and_15_out);
  or or_4 (e, and_16_out, and_17_out);
  or or_5 (f, and_18_out, and_19_out, and_20_out, and_21_out, and_22_out);
  or or_6 (g, and_23_out, and_24_out, and_25_out, and_26_out);
  or or_7 (a, and_1_out, and_2_out, and_3_out, and_4_out, and_5_out, and_6_out);
endmodule

module \가격표시등  (
  input  [7:0] in_1,
  output out_2,
  output out_3,
  output out_4,
  output out_5,
  output out_6,
  output out_7,
  output out_8,
  output out_9,
  output out_10,
  output out_11,
  output out_12,
  output out_13,
  output out_14,
  output out_15,
  output out_16,
  output out_17
);

  wire and_1_out, comparator_2_eq, comparator_3_eq;
  wire [7:0] divider_1_out, divider_1_rem;
  wire [7:4] multiplexer_1_out, multiplexer_2_out;

  Divider divider_1 (.a(in_1), .b(8'ha), .out(divider_1_out), .rem(divider_1_rem));  // open: upper
  Comparator comparator_1 (.a(in_1), .b({8{1'b0}}), .eq(out_10));  // open: gt, lt
  Comparator comparator_2 (.a(divider_1_out), .b({8{1'b0}}), .eq(comparator_2_eq));  // open: gt, lt
  Comparator comparator_3 (.a(divider_1_rem), .b({8{1'b0}}), .eq(comparator_3_eq));  // open: gt, lt
  Multiplexer #(.width(8)) multiplexer_1 (
    .in0(divider_1_out), .in1({8{1'b1}}), .out({multiplexer_1_out, out_2, out_3, out_4, out_5}),
    .sel(comparator_2_eq));  // open: en
  Multiplexer #(.width(8)) multiplexer_2 (
    .in0(divider_1_rem), .in1({8{1'b1}}), .out({multiplexer_2_out, out_6, out_7, out_8, out_9}),
    .sel(and_1_out));  // open: en
  and and_1 (and_1_out, comparator_3_eq, comparator_2_eq);

  assign out_11 = out_10;
  assign out_12 = out_10;
  assign out_13 = out_10;
  assign out_14 = out_10;
  assign out_15 = out_10;
  assign out_16 = out_10;
  assign out_17 = out_10;

  // Notes on the sheet:
  //   가격 표시등
endmodule
